# Fritzing sketch 20.1-lighting-the-tri-color-LED-based-on-CPU-load (saved by Fritzing 0.9.2b)
breadboards: 1

parts:
  RGB_LED = RGB LED (com. cathode, rgb) [package="5 mm [THT]"]
  R4 = Resistor [tolerance=±5% resistance=100 package="0805 [SMD]"]
  R2 = Resistor [tolerance=±5% resistance=100 package="0805 [SMD]"]
  R3 = Resistor [tolerance=±5% resistance=100 package="0805 [SMD]"]
  Raspberry_Pi1 = Raspberry Pi 2

nets:
  N1: RGB_LED.red_anode, R4.Pin_0
  N2: RGB_LED.common_cathode, Raspberry_Pi1.GND
  N3: RGB_LED.green_anode, R2.Pin_0
  N4: RGB_LED.blue_anode, R3.Pin_0
  N5: R4.Pin_1, Raspberry_Pi1.GPIO16
  N6: R2.Pin_1, Raspberry_Pi1.GPIO20
  N7: R3.Pin_1, Raspberry_Pi1.GPIO21

notes:
  RGB LED
